# Fritzing sketch Schematic (saved by Fritzing 0.9.2b)
breadboards: 1

parts:
  Part1 = Arduino Uno (Rev3)
  R1 = Resistor [tolerance=±5% resistance=220 package=THT]
  R2 = Resistor [tolerance=±5% resistance=220 package=THT]
  R3 = Resistor [tolerance=±5% resistance=220 package=THT]
  R4 = Resistor [tolerance=±5% resistance=220 package=THT]
  R5 = Resistor [tolerance=±5% resistance=220 package=THT]
  R6 = Resistor [tolerance=±5% resistance=220 package=THT]
  R7 = Resistor [tolerance=±5% resistance=220 package=THT]
  R8 = Resistor [tolerance=±5% resistance=220 package=THT]
  R9 = Resistor [tolerance=±5% resistance=220 package=THT]
  R10 = Resistor [tolerance=±5% resistance=220 package=THT]
  LED1 = LED - 5mm [color="Red (633nm)" package="5 mm [THT]"]
  LED2 = LED - 5mm [color="Red (633nm)" package="5 mm [THT]"]
  LED3 = LED - 5mm [color="Red (633nm)" package="5 mm [THT]"]
  LED4 = LED - 5mm [color="Red (633nm)" package="5 mm [THT]"]
  LED5 = LED - 5mm [color="Red (633nm)" package="5 mm [THT]"]
  LED6 = LED - 5mm [color="Red (633nm)" package="5 mm [THT]"]
  LED7 = LED - 5mm [color="Red (633nm)" package="5 mm [THT]"]
  LED8 = LED - 5mm [color="Red (633nm)" package="5 mm [THT]"]
  LED9 = LED - 5mm [color="Red (633nm)" package="5 mm [THT]"]
  LED10 = LED - 5mm [color="Red (633nm)" package="5 mm [THT]"]

nets:
  N1: Part1.D8, R7.Pin_0
  N2: Part1.D9_PWM, R8.Pin_0
  N3: Part1.D10_PWM/SS, R9.Pin_0
  N4: Part1.D11_PWM/MOSI, R10.Pin_0
  N5: Part1.D2, R1.Pin_0
  N6: Part1.D3_PWM, R2.Pin_0
  N7: Part1.D4, R3.Pin_0
  N8: Part1.D5_PWM, R4.Pin_0
  N9: Part1.D6_PWM, R5.Pin_0
  N10: Part1.D7, R6.Pin_0
  N11: R1.Pin_1, LED10.anode
  N12: R2.Pin_1, LED9.anode
  N13: R3.Pin_1, LED8.anode
  N14: R4.Pin_1, LED7.anode
  N15: R5.Pin_1, LED6.anode
  N16: R6.Pin_1, LED5.anode
  N17: R7.Pin_1, LED4.anode
  N18: R8.Pin_1, LED3.anode
  N19: R9.Pin_1, LED2.anode
  N20: R10.Pin_1, LED1.anode
  N21: LED1.cathode, LED2.cathode, LED3.cathode, LED4.cathode, LED5.cathode, LED6.cathode, LED7.cathode, LED8.cathode, LED9.cathode, LED10.cathode
