# Fritzing sketch Schematic (saved by Fritzing 0.9.2b)
breadboards: 1

parts:
  Part1 = Arduino Uno (Rev3)
  R1 = Resistor [tolerance=±5% resistance=220 package=THT]
  R2 = Resistor [tolerance=±5% resistance=220 package=THT]
  R3 = Resistor [tolerance=±5% resistance=220 package=THT]
  R4 = Resistor [tolerance=±5% resistance=220 package=THT]
  R5 = Resistor [tolerance=±5% resistance=220 package=THT]
  R6 = Resistor [tolerance=±5% resistance=220 package=THT]
  R7 = Resistor [tolerance=±5% resistance=220 package=THT]
  R8 = Resistor [tolerance=±5% resistance=220 package=THT]
  R9 = Resistor [tolerance=±5% resistance=220 package=THT]
  R10 = Resistor [tolerance=±5% resistance=220 package=THT]
  LED1 = LED - 5mm [color="Red (633nm)" package="5 mm [THT]"]
  LED2 = LED - 5mm [color="Red (633nm)" package="5 mm [THT]"]
  LED3 = LED - 5mm [color="Red (633nm)" package="5 mm [THT]"]
  LED4 = LED - 5mm [color="Red (633nm)" package="5 mm [THT]"]
  LED5 = LED - 5mm [color="Red (633nm)" package="5 mm [THT]"]
  LED6 = LED - 5mm [color="Red (633nm)" package="5 mm [THT]"]
  LED7 = LED - 5mm [color="Red (633nm)" package="5 mm [THT]"]
  LED8 = LED - 5mm [color="Red (633nm)" package="5 mm [THT]"]
  LED9 = LED - 5mm [color="Red (633nm)" package="5 mm [THT]"]
  LED10 = LED - 5mm [color="Red (633nm)" package="5 mm [THT]"]

nets:
  N1: Part1.D8, R7.Pin_0
  N2: Part1.D9_PWM, R8.Pin_0
  N3: Part1.D10_PWM/SS, R9.Pin_0
  N4: Part1.D11_PWM/MOSI, R10.Pin_0
  N5: Part1.GND, LED1.cathode, LED2.cathode, LED3.cathode, LED4.cathode, LED5.cathode, LED6.cathode, LED7.cathode, LED8.cathode, LED9.cathode, LED10.cathode
  N6: Part1.D2, R1.Pin_0
  N7: Part1.D3_PWM, R2.Pin_0
  N8: Part1.D4, R3.Pin_0
  N9: Part1.D5_PWM, R4.Pin_0
  N10: Part1.D6_PWM, R5.Pin_0
  N11: Part1.D7, R6.Pin_0
  N12: R1.Pin_1, LED10.anode
  N13: R2.Pin_1, LED9.anode
  N14: R3.Pin_1, LED8.anode
  N15: R4.Pin_1, LED7.anode
  N16: R5.Pin_1, LED6.anode
  N17: R6.Pin_1, LED5.anode
  N18: R7.Pin_1, LED4.anode
  N19: R8.Pin_1, LED3.anode
  N20: R9.Pin_1, LED2.anode
  N21: R10.Pin_1, LED1.anode

// code stored in the sketch: POVDuino.ino
//List your pins that control lights
int pinA = 2;
int pinB = 3;
int pinC = 4;
int pinD = 5;
int pinE = 6;
int pinF = 7;
int pinG = 8;
int pinH = 9;
int pinI = 10;
int pinJ = 11;

int subletspace = 250;
int letspace = 150;
int wordspace = 500;

void setup() {
  // put your setup code here, to run once:
  pinMode(0, OUTPUT);
  pinMode(1, OUTPUT);
  pinMode(2, OUTPUT);
  pinMode(3, OUTPUT);
  pinMode(4, OUTPUT);
  pinMode(5, OUTPUT);
  pinMode(6, OUTPUT);
  pinMode(7, OUTPUT);
  pinMode(8, OUTPUT);
  pinMode(9, OUTPUT);
  pinMode(10, OUTPUT);
  pinMode(11, OUTPUT);
  pinMode(12, OUTPUT);
  pinMode(13, OUTPUT);
}

//This script allows one to test that all of the LEDs light up properly and then the orientation. If executed correctly, all LEDs should flash and then the top LED should stay on.
//If the bottom LED illuminates instead of the top, replace values (i.e change pinA to pinJ and pinB to pinI and so on).
void configuration() {
  digitalWrite(pinA, HIGH);
  digitalWrite(pinB, HIGH);
  digitalWrite(pinC, HIGH);
  digitalWrite(pinD, HIGH);
  digitalWrite(pinE, HIGH);
  digitalWrite(pinF, HIGH);
  digitalWrite(pinG, HIGH);
  digitalWrite(pinH, HIGH);
  digitalWrite(pinI, HIGH);
  digitalWrite(pinJ, HIGH);
  delay(wordspace);
  digitalWrite(pinA, LOW);
  digitalWrite(pinB, LOW);
  digitalWrite(pinC, LOW);
  digitalWrite(pinD, LOW);
  digitalWrite(pinE, LOW);
  digitalWrite(pinF, LOW);
  digitalWrite(pinG, LOW);
  digitalWrite(pinH, LOW);
  digitalWrite(pinI, LOW);
  digitalWrite(pinJ, LOW);
  delay(wordspace);
  digitalWrite(pinJ, HIGH);
  delay(wordspace*2);
  digitalWrite(pinJ, LOW);
  
}
  
void printA() {
  digitalWrite(pinA, HIGH);
  delay(subletspace);
  digitalWrite(pinA, LOW);
  digitalWrite(pinB, HIGH);
  delay(subletspace);
  digitalWrite(pinB, LOW);
  digitalWrite(pinC, HIGH);
  delay(subletspace);
  digitalWrite(pinC, LOW);
  digitalWrite(pinD, HIGH);
  delay(subletspace);
  digitalWrite(pinD, LOW);
  digitalWrite(pinE, HIGH);
  delay(subletspace);
  digitalWrite(pinF, HIGH);
  delay(subletspace);
  digitalWrite(pinF, LOW);
  digitalWrite(pinG, HIGH);
  delay(subletspace);
  digitalWrite(pinG, LOW);
  digitalWrite(pinH, HIGH);
  delay(subletspace);
  digitalWrite(pinH, LOW);
  digitalWrite(pinI, HIGH);
  delay(subletspace);
  digitalWrite(pinI, LOW);
  digitalWrite(pinJ, HIGH);
  delay(subletspace);
  digitalWrite(pinJ, LOW);
  digitalWrite(pinI, HIGH);
  delay(subletspace);
  digitalWrite(pinI, LOW);
  digitalWrite(pinH, HIGH);
  delay(subletspace);
  digitalWrite(pinH, LOW);
  digitalWrite(pinG, HIGH);
  delay(subletspace);
  digitalWrite(pinG, LOW);
  digitalWrite(pinF, HIGH);
  delay(subletspace);
  digitalWrite(pinF, LOW);
  delay(subletspace);
  digitalWrite(pinE, LOW);
  digitalWrite(pinD, HIGH);
  delay(subletspace);
  digitalWrite(pinD, LOW);
  digitalWrite(pinC, HIGH);
  delay(subletspace);
  digitalWrite(pinC, LOW);
  digitalWrite(pinB, HIGH);
  delay(subletspace);
  digitalWrite(pinB, LOW);
  digitalWrite(pinA, HIGH);
  delay(subletspace);
  digitalWrite(pinA, LOW);
}

void printB() {
  digitalWrite(pinA, HIGH);
  digitalWrite(pinB, HIGH);
  digitalWrite(pinC, HIGH);
  digitalWrite(pinD, HIGH);
  digitalWrite(pinE, HIGH);
  digitalWrite(pinF, HIGH);
  digitalWrite(pinG, HIGH);
  digitalWrite(pinH, HIGH);
  digitalWrite(pinI, HIGH);
  digitalWrite(pinJ, HIGH);
  delay(subletspace);
  digitalWrite(pinA, HIGH);
  digitalWrite(pinB, LOW);
  digitalWrite(pinC, LOW);
  digitalWrite(pinD, LOW);
  digitalWrite(pinE, LOW);
  digitalWrite(pinF, LOW);
  digitalWrite(pinG, LOW);
  digitalWrite(pinH, LOW);
  digitalWrite(pinI, LOW);
  digitalWrite(pinJ, LOW);
  delay(subletspace);
  digitalWrite(pinJ, HIGH);
  digitalWrite(pinF, HIGH);
  digitalWrite(pinA, HIGH);
  delay(5*subletspace);
  digitalWrite(pinA, LOW);
  digitalWrite(pinF, LOW);
  digitalWrite(pinJ, LOW);
  delay(subletspace);
  digitalWrite(pinI, HIGH);
  digitalWrite(pinH, HIGH);
  digitalWrite(pinG, HIGH);
  digitalWrite(pinE, HIGH);
  digitalWrite(pinD, HIGH);
  digitalWrite(pinC, HIGH);
  digitalWrite(pinB, HIGH);
  delay(subletspace);
  digitalWrite(pinI, LOW);
  digitalWrite(pinH, LOW);
  digitalWrite(pinG, LOW);
  digitalWrite(pinE, LOW);
  digitalWrite(pinD, LOW);
  digitalWrite(pinC, LOW);
  digitalWrite(pinB, LOW);
  delay(subletspace);
}

void printC() {
  digitalWrite(pinB, HIGH);
  digitalWrite(pinC, HIGH);
  digitalWrite(pinD, HIGH);
  digitalWrite(pinE, HIGH);
  digitalWrite(pinF, HIGH);
  digitalWrite(pinG, HIGH);
  digitalWrite(pinH, HIGH);
  digitalWrite(pinI, HIGH);
  delay(subletspace);
  digitalWrite(pinB, LOW);
  digitalWrite(pinC, LOW);
  digitalWrite(pinD, LOW);
  digitalWrite(pinE, LOW);
  digitalWrite(pinF, LOW);
  digitalWrite(pinG, LOW);
  digitalWrite(pinH, LOW);
  digitalWrite(pinI, LOW);
  delay(subletspace);
  digitalWrite(pinJ, HIGH);
  digitalWrite(pinA, HIGH);
  delay(6*subletspace);
  digitalWrite(pinA, LOW);
  digitalWrite(pinJ, LOW);
}

void printD() {
  digitalWrite(pinA, HIGH);
  digitalWrite(pinB, HIGH);
  digitalWrite(pinC, HIGH);
  digitalWrite(pinD, HIGH);
  digitalWrite(pinE, HIGH);
  digitalWrite(pinF, HIGH);
  digitalWrite(pinG, HIGH);
  digitalWrite(pinH, HIGH);
  digitalWrite(pinI, HIGH);
  digitalWrite(pinJ, HIGH);
  delay(subletspace);
  digitalWrite(pinI, LOW);
  digitalWrite(pinH, LOW);
  digitalWrite(pinG, LOW);
  digitalWrite(pinF, LOW);
  digitalWrite(pinE, LOW);
  digitalWrite(pinD, LOW);
  digitalWrite(pinC, LOW);
  digitalWrite(pinB, LOW);
  delay(subletspace);
  digitalWrite(pinA, LOW);
  digitalWrite(pinB, HIGH);
  delay(subletspace);
  digitalWrite(pinB, LOW);
  digitalWrite(pinC, HIGH);
  delay(subletspace);
  digitalWrite(pinC, LOW);
  digitalWrite(pinD, HIGH);
  delay(subletspace);
  digitalWrite(pinD, LOW);
  digitalWrite(pinE, HIGH);
  delay(subletspace);
  digitalWrite(pinE, LOW);
  digitalWrite(pinF, HIGH);
  delay(subletspace);
  digitalWrite(pinF, LOW);
  digitalWrite(pinG, HIGH);
  delay(subletspace);
  digitalWrite(pinG, LOW);
  digitalWrite(pinH, HIGH);
  delay(subletspace);
  digitalWrite(pinH, LOW);
  digitalWrite(pinI, HIGH);
  digitalWrite(pinJ, LOW);
  delay(subletspace);
  digitalWrite(pinI, LOW);
}

void printE() {
  digitalWrite(pinA, HIGH);
  digitalWrite(pinB, HIGH);
  digitalWrite(pinC, HIGH);
  digitalWrite(pinD, HIGH);
  digitalWrite(pinE, HIGH);
  digitalWrite(pinF, HIGH);
  digitalWrite(pinG, HIGH);
  digitalWrite(pinH, HIGH);
  digitalWrite(pinI, HIGH);
  digitalWrite(pinJ, HIGH);
  delay(subletspace);
  digitalWrite(pinB, LOW);
  digitalWrite(pinC, LOW);
  digitalWrite(pinD, LOW);
  digitalWrite(pinE, LOW);
  digitalWrite(pinG, LOW);
  digitalWrite(pinH, LOW);
  digitalWrite(pinI, LOW);
  delay(6*subletspace);
}

void printF() {
  digitalWrite(pinA, HIGH);
  digitalWrite(pinB, HIGH);
  digitalWrite(pinC, HIGH);
  digitalWrite(pinD, HIGH);
  digitalWrite(pinE, HIGH);
  digitalWrite(pinF, HIGH);
  digitalWrite(pinG, HIGH);
  digitalWrite(pinH, HIGH);
  digitalWrite(pinI, HIGH);
  digitalWrite(pinJ, HIGH);
  delay(subletspace);
  digitalWrite(pinA, LOW);
  digitalWrite(pinB, LOW);
  digitalWrite(pinC, LOW);
  digitalWrite(pinD, LOW);
  digitalWrite(pinE, LOW);
  digitalWrite(pinG, LOW);
  digitalWrite(pinH, LOW);
  digitalWrite(pinI, LOW);
  delay(6*subletspace);
}

void printG() {
  digitalWrite(pinF, HIGH);
  delay(subletspace);
  digitalWrite(pinF, LOW);
  digitalWrite(pinG, HIGH);
  digitalWrite(pinE, HIGH);
  delay(subletspace);
  digitalWrite(pinE, LOW);
  digitalWrite(pinG, LOW);
  digitalWrite(pinH, HIGH);
  digitalWrite(pinD, HIGH);
  delay(subletspace);
  digitalWrite(pinD, LOW);
  digitalWrite(pinH, LOW);
  digitalWrite(pinI, HIGH);
  digitalWrite(pinC, HIGH);
  delay(subletspace);
  digitalWrite(pinC, LOW);
  digitalWrite(pinI, LOW);
  digitalWrite(pinB, HIGH);
  digitalWrite(pinJ, HIGH);
  delay(subletspace);
  digitalWrite(pinB, LOW);
  digitalWrite(pinA, HIGH);
  digitalWrite(pinF, HIGH);
  delay(3*subletspace);
  digitalWrite(pinF, LOW);
  digitalWrite(pinB, HIGH);
  digitalWrite(pinC, HIGH);
  digitalWrite(pinD, HIGH);
  digitalWrite(pinE, HIGH);
  delay(subletspace);
  digitalWrite(pinE, LOW);
  digitalWrite(pinC, LOW);
  digitalWrite(pinB, LOW);
  digitalWrite(pinA, LOW);
}

void printH() {
  digitalWrite(pinA, HIGH);
  digitalWrite(pinB, HIGH);
  digitalWrite(pinC, HIGH);
  digitalWrite(pinD, HIGH);
  digitalWrite(pinE, HIGH);
  digitalWrite(pinF, HIGH);
  digitalWrite(pinG, HIGH);
  digitalWrite(pinH, HIGH);
  digitalWrite(pinI, HIGH);
  digitalWrite(pinJ, HIGH);
  delay(subletspace);
  digitalWrite(pinA, LOW);
  digitalWrite(pinB, LOW);
  digitalWrite(pinC, LOW);
  digitalWrite(pinD, LOW);
  digitalWrite(pinE, LOW);
  digitalWrite(pinG, LOW);
  digitalWrite(pinH, LOW);
  digitalWrite(pinI, LOW);
  digitalWrite(pinJ, LOW);
  delay(subletspace*5);
  digitalWrite(pinA, HIGH);
  digitalWrite(pinB, HIGH);
  digitalWrite(pinC, HIGH);
  digitalWrite(pinD, HIGH);
  digitalWrite(pinE, HIGH);
  digitalWrite(pinF, HIGH);
  digitalWrite(pinG, HIGH);
  digitalWrite(pinH, HIGH);
  digitalWrite(pinI, HIGH);
  digitalWrite(pinJ, HIGH);
  delay(subletspace);
  digitalWrite(pinA, LOW);
  digitalWrite(pinB, LOW);
  digitalWrite(pinC, LOW);
  digitalWrite(pinD, LOW);
  digitalWrite(pinF, LOW);
  digitalWrite(pinE, LOW);
  digitalWrite(pinG, LOW);
  digitalWrite(pinH, LOW);
  digitalWrite(pinI, LOW);
  digitalWrite(pinJ, LOW);
}

void printI() {
  digitalWrite(pinJ, HIGH);
  digitalWrite(pinA, HIGH);
  delay(subletspace*3);
  digitalWrite(pinB, HIGH);
  digitalWrite(pinC, HIGH);
  digitalWrite(pinD, HIGH);
  digitalWrite(pinE, HIGH);
  digitalWrite(pinF, HIGH);
  digitalWrite(pinG, HIGH);
  digitalWrite(pinH, HIGH);
  digitalWrite(pinI, HIGH);
  delay(subletspace);
  digitalWrite(pinB, LOW);
  digitalWrite(pinC, LOW);
  digitalWrite(pinD, LOW);
  digitalWrite(pinE, LOW);
  digitalWrite(pinF, LOW);
  digitalWrite(pinG, LOW);
  digitalWrite(pinH, LOW);
  digitalWrite(pinI, LOW);
  delay(subletspace*3);
  digitalWrite(pinA, LOW);
  digitalWrite(pinJ, LOW);
}

void printJ() {
  digitalWrite(pinE, HIGH);
  delay(subletspace);
  digitalWrite(pinE, LOW);
  digitalWrite(pinD, HIGH);
  delay(subletspace);
  digitalWrite(pinD, LOW);
  digitalWrite(pinC, HIGH);
  digitalWrite(pinJ, HIGH);
  delay(subletspace);
  digitalWrite(pinC, LOW); 
  digitalWrite(pinB, HIGH);
  delay(subletspace);
  digitalWrite(pinB, LOW);
  digitalWrite(pinA, HIGH);
  delay(subletspace); 
  digitalWrite(pinB, HIGH);
  digitalWrite(pinC, HIGH);
  digitalWrite(pinD, HIGH);
  digitalWrite(pinE, HIGH);
  digitalWrite(pinF, HIGH);
  digitalWrite(pinG, HIGH);
  digitalWrite(pinH, HIGH);
  digitalWrite(pinI, HIGH);
  delay(subletspace);
  digitalWrite(pinA, LOW);
  digitalWrite(pinB, LOW);
  digitalWrite(pinC, LOW);
  digitalWrite(pinD, LOW);
  digitalWrite(pinE, LOW);
  digitalWrite(pinF, LOW);
  digitalWrite(pinG, LOW);
  digitalWrite(pinH, LOW);
  digitalWrite(pinI, LOW);
  delay(subletspace*3);
  digitalWrite(pinJ, LOW);
}

void printK() {
  digitalWrite(pinA, HIGH);
  digitalWrite(pinB, HIGH);
  digitalWrite(pinC, HIGH);
  digitalWrite(pinD, HIGH);
  digitalWrite(pinE, HIGH);
  digitalWrite(pinF, HIGH);
  digitalWrite(pinG, HIGH);
  digitalWrite(pinH, HIGH);
  digitalWrite(pinI, HIGH);
  digitalWrite(pinJ, HIGH);
  delay(subletspace);
  digitalWrite(pinA, LOW);
  digitalWrite(pinB, LOW);
  digitalWrite(pinC, LOW);
  digitalWrite(pinD, LOW);
  digitalWrite(pinE, LOW);
  digitalWrite(pinG, LOW);
  digitalWrite(pinH, LOW);
  digitalWrite(pinI, LOW);
  digitalWrite(pinJ, LOW);
  delay(subletspace);
  digitalWrite(pinF, LOW);
  digitalWrite(pinG, HIGH);
  digitalWrite(pinE, HIGH);
  delay(subletspace);
  digitalWrite(pinE, LOW);
  digitalWrite(pinG, LOW);
  digitalWrite(pinH, HIGH);
  digitalWrite(pinD, HIGH);
  delay(subletspace);
  digitalWrite(pinD, LOW);
  digitalWrite(pinH, LOW);
  digitalWrite(pinI, HIGH);
  digitalWrite(pinC, HIGH);
  delay(subletspace);
  digitalWrite(pinC, LOW);
  digitalWrite(pinI, LOW);
  digitalWrite(pinJ, HIGH);
  digitalWrite(pinB, HIGH);
  delay(subletspace);
  digitalWrite(pinB, LOW);
  digitalWrite(pinJ, LOW);
  digitalWrite(pinA, HIGH);
  delay(subletspace);
  digitalWrite(pinA, LOW);
}

void printL() {
  digitalWrite(pinA, HIGH);
  digitalWrite(pinB, HIGH);
  digitalWrite(pinC, HIGH);
  digitalWrite(pinD, HIGH);
  digitalWrite(pinE, HIGH);
  digitalWrite(pinF, HIGH);
  digitalWrite(pinG, HIGH);
  digitalWrite(pinH, HIGH);
  digitalWrite(pinI, HIGH);
  digitalWrite(pinJ, HIGH);
  delay(subletspace);
  digitalWrite(pinA, LOW);
  digitalWrite(pinB, LOW);
  digitalWrite(pinC, LOW);
  digitalWrite(pinD, LOW);
  digitalWrite(pinE, LOW);
  digitalWrite(pinF, LOW);
  digitalWrite(pinG, LOW);
  digitalWrite(pinH, LOW);
  digitalWrite(pinI, LOW);
  digitalWrite(pinJ, LOW);
  delay(subletspace);
  digitalWrite(pinA, HIGH);
  delay(subletspace*6);
  digitalWrite(pinA, LOW);
}

void printM() {
  digitalWrite(pinA, HIGH);
  digitalWrite(pinB, HIGH);
  digitalWrite(pinC, HIGH);
  digitalWrite(pinD, HIGH);
  digitalWrite(pinE, HIGH);
  digitalWrite(pinF, HIGH);
  digitalWrite(pinG, HIGH);
  digitalWrite(pinH, HIGH);
  digitalWrite(pinI, HIGH);
  digitalWrite(pinJ, HIGH);
  delay(subletspace);
  digitalWrite(pinA, LOW);
  digitalWrite(pinB, LOW);
  digitalWrite(pinC, LOW);
  digitalWrite(pinD, LOW);
  digitalWrite(pinE, LOW);
  digitalWrite(pinF, LOW);
  digitalWrite(pinG, LOW);
  digitalWrite(pinH, LOW);
  digitalWrite(pinJ, LOW);
  delay(subletspace);
  digitalWrite(pinI, LOW);
  digitalWrite(pinH, HIGH);
  delay(subletspace);
  digitalWrite(pinH, LOW);
  digitalWrite(pinG, HIGH);
  delay(subletspace);
  digitalWrite(pinG, LOW);
  digitalWrite(pinF, HIGH);
  delay(subletspace);
  digitalWrite(pinF, LOW);
  digitalWrite(pinE, HIGH);
  delay(subletspace);
  digitalWrite(pinE, LOW);
  digitalWrite(pinD, HIGH);
  delay(subletspace);
  digitalWrite(pinD, LOW);
  digitalWrite(pinE, HIGH);
  delay(subletspace);
  digitalWrite(pinE, LOW);
  digitalWrite(pinF, HIGH);
  delay(subletspace);
  digitalWrite(pinF, LOW);
  digitalWrite(pinG, HIGH);
  delay(subletspace);
  digitalWrite(pinG, LOW);
  digitalWrite(pinH, HIGH);
  delay(subletspace);
  digitalWrite(pinH, LOW);
  digitalWrite(pinI, HIGH);
  delay(subletspace);
  digitalWrite(pinA, HIGH);
  digitalWrite(pinB, HIGH);
  digitalWrite(pinC, HIGH);
  digitalWrite(pinD, HIGH);
  digitalWrite(pinE, HIGH);
  digitalWrite(pinF, HIGH);
  digitalWrite(pinG, HIGH);
  digitalWrite(pinH, HIGH);
  digitalWrite(pinI, HIGH);
  digitalWrite(pinJ, HIGH);
  delay(subletspace);
  digitalWrite(pinA, LOW);
  digitalWrite(pinB, LOW);
  digitalWrite(pinC, LOW);
  digitalWrite(pinD, LOW);
  digitalWrite(pinE, LOW);
  digitalWrite(pinF, LOW);
  digitalWrite(pinG, LOW);
  digitalWrite(pinH, LOW);
  digitalWrite(pinI, LOW);
  digitalWrite(pinJ, LOW);
}   
 
void printN() {
  digitalWrite(pinA, HIGH);
  digitalWrite(pinB, HIGH);
  digitalWrite(pinC, HIGH);
  digitalWrite(pinD, HIGH);
  digitalWrite(pinE, HIGH);
  digitalWrite(pinF, HIGH);
  digitalWrite(pinG, HIGH);
  digitalWrite(pinH, HIGH);
  digitalWrite(pinI, HIGH);
  digitalWrite(pinJ, HIGH);
  delay(subletspace);
  digitalWrite(pinA, LOW);
  digitalWrite(pinB, LOW);
  digitalWrite(pinC, LOW);
  digitalWrite(pinD, LOW);
  digitalWrite(pinE, LOW);
  digitalWrite(pinF, LOW);
  digitalWrite(pinG, LOW);
  digitalWrite(pinH, LOW);
  digitalWrite(pinJ, LOW);
  delay(subletspace);
  digitalWrite(pinI, LOW);
  digitalWrite(pinH, HIGH);
  delay(subletspace);
  digitalWrite(pinH, LOW);
  digitalWrite(pinG, HIGH);
  delay(subletspace);
  digitalWrite(pinG, LOW);
  digitalWrite(pinF, HIGH);
  delay(subletspace);
  digitalWrite(pinF, LOW);
  digitalWrite(pinE, HIGH);
  delay(subletspace);
  digitalWrite(pinE, LOW);
  digitalWrite(pinD, HIGH);
  delay(subletspace);
  digitalWrite(pinD, LOW);
  digitalWrite(pinC, HIGH);
  delay(subletspace);
  digitalWrite(pinA, HIGH);
  digitalWrite(pinB, HIGH);
  digitalWrite(pinD, HIGH);
  digitalWrite(pinE, HIGH);
  digitalWrite(pinF, HIGH);
  digitalWrite(pinG, HIGH);
  digitalWrite(pinH, HIGH);
  digitalWrite(pinI, HIGH);
  digitalWrite(pinJ, HIGH);
  delay(subletspace);
  digitalWrite(pinA, LOW);
  digitalWrite(pinB, LOW);
  digitalWrite(pinC, LOW);
  digitalWrite(pinD, LOW);
  digitalWrite(pinE, LOW);
  digitalWrite(pinF, LOW);
  digitalWrite(pinG, LOW);
  digitalWrite(pinH, LOW);
  digitalWrite(pinI, LOW);
  digitalWrite(pinJ, LOW);
}

void printO() {
  digitalWrite(pinB, HIGH);
  digitalWrite(pinC, HIGH);
  digitalWrite(pinD, HIGH);
  digitalWrite(pinE, HIGH);
  digitalWrite(pinF, HIGH);
  digitalWrite(pinG, HIGH);
  digitalWrite(pinH, HIGH);
  digitalWrite(pinI, HIGH);
  delay(subletspace);
  digitalWrite(pinB, LOW);
  digitalWrite(pinC, LOW);
  digitalWrite(pinD, LOW);
  digitalWrite(pinE, LOW);
  digitalWrite(pinF, LOW);
  digitalWrite(pinG, LOW);
  digitalWrite(pinH, LOW);
  digitalWrite(pinI, LOW);
  delay(subletspace);
  digitalWrite(pinJ, HIGH);
  digitalWrite(pinA, HIGH);
  delay(subletspace*8);
  digitalWrite(pinJ, LOW);
  digitalWrite(pinA, LOW);
  digitalWrite(pinB, HIGH);
  digitalWrite(pinC, HIGH);
  digitalWrite(pinD, HIGH);
  digitalWrite(pinE, HIGH);
  digitalWrite(pinF, HIGH);
  digitalWrite(pinG, HIGH);
  digitalWrite(pinH, HIGH);
  digitalWrite(pinI, HIGH);
  delay(subletspace);
  digitalWrite(pinB, LOW);
  digitalWrite(pinC, LOW);
  digitalWrite(pinD, LOW);
  digitalWrite(pinE, LOW);
  digitalWrite(pinF, LOW);
  digitalWrite(pinG, LOW);
  digitalWrite(pinH, LOW);
  digitalWrite(pinI, LOW);
}

void printP(){
  digitalWrite(pinA, HIGH);
  digitalWrite(pinB, HIGH);
  digitalWrite(pinC, HIGH);
  digitalWrite(pinD, HIGH);
  digitalWrite(pinE, HIGH);
  digitalWrite(pinF, HIGH);
  digitalWrite(pinG, HIGH);
  digitalWrite(pinH, HIGH);
  digitalWrite(pinI, HIGH);
  digitalWrite(pinJ, HIGH);
  delay(subletspace);
  digitalWrite(pinA, LOW);
  digitalWrite(pinB, LOW);
  digitalWrite(pinC, LOW);
  digitalWrite(pinD, LOW);
  digitalWrite(pinE, LOW);
  digitalWrite(pinG, LOW);
  digitalWrite(pinH, LOW);
  digitalWrite(pinI, LOW);
  delay(subletspace*3);
  digitalWrite(pinI, HIGH);
  digitalWrite(pinH, HIGH);
  digitalWrite(pinG, HIGH);
  delay(subletspace);
  digitalWrite(pinF, LOW);
  digitalWrite(pinG, LOW);
  digitalWrite(pinH, LOW);
  digitalWrite(pinI, LOW);
  digitalWrite(pinJ, LOW);
  delay(subletspace);
}

void printQ() {
  digitalWrite(pinB, HIGH);
  digitalWrite(pinC, HIGH);
  digitalWrite(pinD, HIGH);
  digitalWrite(pinE, HIGH);
  digitalWrite(pinF, HIGH);
  digitalWrite(pinG, HIGH);
  digitalWrite(pinH, HIGH);
  digitalWrite(pinI, HIGH);
  delay(subletspace);
  digitalWrite(pinB, LOW);
  digitalWrite(pinC, LOW);
  digitalWrite(pinD, LOW);
  digitalWrite(pinE, LOW);
  digitalWrite(pinF, LOW);
  digitalWrite(pinG, LOW);
  digitalWrite(pinH, LOW);
  digitalWrite(pinI, LOW);
  delay(subletspace);
  digitalWrite(pinA, HIGH);
  digitalWrite(pinJ, HIGH);
  delay(subletspace*5);
  digitalWrite(pinB, HIGH);
  delay(subletspace);
  digitalWrite(pinJ, LOW);
  digitalWrite(pinC, HIGH);
  digitalWrite(pinD, HIGH);
  digitalWrite(pinE, HIGH);
  digitalWrite(pinF, HIGH);
  digitalWrite(pinG, HIGH);
  digitalWrite(pinH, HIGH);
  digitalWrite(pinI, HIGH);
  delay(subletspace);
  digitalWrite(pinB, LOW);
  digitalWrite(pinC, LOW);
  digitalWrite(pinD, LOW);
  digitalWrite(pinE, LOW);
  digitalWrite(pinF, LOW);
  digitalWrite(pinG, LOW);
  digitalWrite(pinH, LOW);
  digitalWrite(pinI, LOW);
  digitalWrite(pinJ, LOW);
  delay(subletspace);
  digitalWrite(pinA, LOW);
  delay(subletspace);
}
  
void printR(){
  digitalWrite(pinA, HIGH);
  digitalWrite(pinB, HIGH);
  digitalWrite(pinC, HIGH);
  digitalWrite(pinD, HIGH);
  digitalWrite(pinE, HIGH);
  digitalWrite(pinF, HIGH);
  digitalWrite(pinG, HIGH);
  digitalWrite(pinH, HIGH);
  digitalWrite(pinI, HIGH);
  digitalWrite(pinJ, HIGH);
  delay(subletspace);
  digitalWrite(pinA, LOW);
  digitalWrite(pinB, LOW);
  digitalWrite(pinC, LOW);
  digitalWrite(pinD, LOW);
  digitalWrite(pinG, LOW);
  digitalWrite(pinH, LOW);
  digitalWrite(pinI, LOW);
  delay(subletspace);
  digitalWrite(pinE, LOW);
  digitalWrite(pinD, HIGH);
  delay(subletspace);
  digitalWrite(pinD, LOW);
  digitalWrite(pinC, HIGH);
  delay(subletspace);
  digitalWrite(pinI, HIGH);
  digitalWrite(pinH, HIGH);
  digitalWrite(pinG, HIGH);
  digitalWrite(pinC, LOW);
  digitalWrite(pinB, HIGH);
  delay(subletspace);
  digitalWrite(pinB, LOW);
  digitalWrite(pinA, HIGH);
  digitalWrite(pinF, LOW);
  digitalWrite(pinG, LOW);
  digitalWrite(pinH, LOW);
  digitalWrite(pinI, LOW);
  digitalWrite(pinJ, LOW);
  delay(subletspace);
  digitalWrite(pinA, LOW);
  delay(subletspace);
}  

void printS() {
  digitalWrite(pinA, HIGH);
  digitalWrite(pinG, HIGH);
  digitalWrite(pinH, HIGH);
  digitalWrite(pinI, HIGH);
  delay(subletspace);
  digitalWrite(pinJ, HIGH);
  digitalWrite(pinF, HIGH);
  digitalWrite(pinG, LOW);
  digitalWrite(pinH, LOW);
  digitalWrite(pinI, LOW);
  delay(subletspace*3);
  digitalWrite(pinA, LOW);
  digitalWrite(pinF, LOW);
  digitalWrite(pinB, HIGH);
  digitalWrite(pinC, HIGH);
  digitalWrite(pinD, HIGH);
  digitalWrite(pinE, HIGH);
  delay(subletspace);
  digitalWrite(pinB, LOW);
  digitalWrite(pinC, LOW);
  digitalWrite(pinD, LOW);
  digitalWrite(pinE, LOW);
  delay(subletspace);
  digitalWrite(pinJ, LOW);
  delay(subletspace);
}

void printT() {
  digitalWrite(pinJ, HIGH);
  delay(subletspace*4);
  digitalWrite(pinA, HIGH);
  digitalWrite(pinB, HIGH);
  digitalWrite(pinC, HIGH);
  digitalWrite(pinD, HIGH);
  digitalWrite(pinE, HIGH);
  digitalWrite(pinF, HIGH);
  digitalWrite(pinG, HIGH);
  digitalWrite(pinH, HIGH);
  digitalWrite(pinI, HIGH);
  delay(subletspace);
  digitalWrite(pinA, LOW);
  digitalWrite(pinB, LOW);
  digitalWrite(pinC, LOW);
  digitalWrite(pinD, LOW);
  digitalWrite(pinE, LOW);
  digitalWrite(pinF, LOW);
  digitalWrite(pinG, LOW);
  digitalWrite(pinH, LOW);
  digitalWrite(pinI, LOW);
  delay(subletspace*5);
  digitalWrite(pinJ, LOW);
  delay(subletspace);
}

void printU() {
  digitalWrite(pinB, HIGH);
  digitalWrite(pinC, HIGH);
  digitalWrite(pinD, HIGH);
  digitalWrite(pinE, HIGH);
  digitalWrite(pinF, HIGH);
  digitalWrite(pinG, HIGH);
  digitalWrite(pinH, HIGH);
  digitalWrite(pinI, HIGH);
  digitalWrite(pinJ, HIGH);
  delay(subletspace);
  digitalWrite(pinB, LOW);
  digitalWrite(pinC, LOW);
  digitalWrite(pinD, LOW);
  digitalWrite(pinE, LOW);
  digitalWrite(pinF, LOW);
  digitalWrite(pinG, LOW);
  digitalWrite(pinH, LOW);
  digitalWrite(pinI, LOW);
  digitalWrite(pinJ, LOW);
  digitalWrite(pinA, HIGH);
  delay(subletspace*6);
  digitalWrite(pinA, LOW);
  digitalWrite(pinB, HIGH);
  digitalWrite(pinC, HIGH);
  digitalWrite(pinD, HIGH);
  digitalWrite(pinE, HIGH);
  digitalWrite(pinF, HIGH);
  digitalWrite(pinG, HIGH);
  digitalWrite(pinH, HIGH);
  digitalWrite(pinI, HIGH);
  digitalWrite(pinJ, HIGH);
  delay(subletspace);
  digitalWrite(pinB, LOW);
  digitalWrite(pinC, LOW);
  digitalWrite(pinD, LOW);
  digitalWrite(pinE, LOW);
  digitalWrite(pinF, LOW);
  digitalWrite(pinG, LOW);
  digitalWrite(pinH, LOW);
  digitalWrite(pinI, LOW);
  digitalWrite(pinJ, LOW);
  delay(subletspace);
}

void printV() {
  digitalWrite(pinJ, HIGH);
  delay(subletspace);
  digitalWrite(pinJ, LOW);
  digitalWrite(pinI, HIGH);
  delay(subletspace);
  digitalWrite(pinI, LOW);
  digitalWrite(pinH, HIGH);
  delay(subletspace);
  digitalWrite(pinH, LOW);
  digitalWrite(pinG, HIGH);
  delay(subletspace);
  digitalWrite(pinG, LOW);
  digitalWrite(pinF, HIGH);
  delay(subletspace);
  digitalWrite(pinF, LOW);
  delay(subletspace);
  digitalWrite(pinE, LOW);
  digitalWrite(pinD, HIGH);
  delay(subletspace);
  digitalWrite(pinD, LOW);
  digitalWrite(pinC, HIGH);
  delay(subletspace);
  digitalWrite(pinC, LOW);
  digitalWrite(pinB, HIGH);
  delay(subletspace);
  digitalWrite(pinB, LOW);
  digitalWrite(pinA, HIGH);
  delay(subletspace);
  digitalWrite(pinA, LOW);
  digitalWrite(pinB, HIGH);
  delay(subletspace);
  digitalWrite(pinB, LOW);
  digitalWrite(pinC, HIGH);
  delay(subletspace);
  digitalWrite(pinC, LOW);
  digitalWrite(pinD, HIGH);
  delay(subletspace);
  digitalWrite(pinD, LOW);
  digitalWrite(pinE, HIGH);
  delay(subletspace);
  digitalWrite(pinF, HIGH);
  delay(subletspace);
  digitalWrite(pinF, LOW);
  digitalWrite(pinG, HIGH);
  delay(subletspace);
  digitalWrite(pinG, LOW);
  digitalWrite(pinH, HIGH);
  delay(subletspace);
  digitalWrite(pinH, LOW);
  digitalWrite(pinI, HIGH);
  delay(subletspace);
  digitalWrite(pinI, LOW);
  digitalWrite(pinJ, HIGH);
  delay(subletspace);
  digitalWrite(pinJ, LOW);
  delay(subletspace);
}

void printW() {
  digitalWrite(pinA, HIGH);
  digitalWrite(pinB, HIGH);
  digitalWrite(pinC, HIGH);
  digitalWrite(pinD, HIGH);
  digitalWrite(pinE, HIGH);
  digitalWrite(pinF, HIGH);
  digitalWrite(pinG, HIGH);
  digitalWrite(pinH, HIGH);
  digitalWrite(pinI, HIGH);
  digitalWrite(pinJ, HIGH);
  delay(subletspace);
  digitalWrite(pinA, LOW);
  digitalWrite(pinB, HIGH);
  digitalWrite(pinC, LOW);
  digitalWrite(pinD, LOW);
  digitalWrite(pinE, LOW);
  digitalWrite(pinF, LOW);
  digitalWrite(pinG, LOW);
  digitalWrite(pinH, LOW);
  digitalWrite(pinI, LOW);
  digitalWrite(pinJ, LOW);
  delay(subletspace);
  digitalWrite(pinB, LOW);
  digitalWrite(pinC, HIGH);
  delay(subletspace);
  digitalWrite(pinC, LOW);
  digitalWrite(pinD, HIGH);
  delay(subletspace);
  digitalWrite(pinD, LOW);
  digitalWrite(pinE, HIGH);
  delay(subletspace);
  digitalWrite(pinF, HIGH);
  delay(subletspace);
  digitalWrite(pinF, LOW);
  digitalWrite(pinG, HIGH);
  delay(subletspace);
  digitalWrite(pinG, LOW);
  digitalWrite(pinH, HIGH);
  delay(subletspace*2);
  digitalWrite(pinH, LOW);
  digitalWrite(pinG, HIGH);
  delay(subletspace);
  digitalWrite(pinG, LOW);
  digitalWrite(pinF, HIGH);
  delay(subletspace);
  digitalWrite(pinF, LOW);
  delay(subletspace);
  digitalWrite(pinE, LOW);
  digitalWrite(pinD, HIGH);
  delay(subletspace);
  digitalWrite(pinD, LOW);
  digitalWrite(pinC, HIGH);
  delay(subletspace);
  digitalWrite(pinC, LOW);
  digitalWrite(pinB, HIGH);
  delay(subletspace);
  digitalWrite(pinB, LOW);
  digitalWrite(pinA, HIGH);
  delay(subletspace);
  digitalWrite(pinA, HIGH);
  digitalWrite(pinB, HIGH);
  digitalWrite(pinC, HIGH);
  digitalWrite(pinD, HIGH);
  digitalWrite(pinE, HIGH);
  digitalWrite(pinF, HIGH);
  digitalWrite(pinG, HIGH);
  digitalWrite(pinH, HIGH);
  digitalWrite(pinI, HIGH);
  digitalWrite(pinJ, HIGH);
  delay(subletspace);
  digitalWrite(pinA, LOW);
  digitalWrite(pinB, LOW);
  digitalWrite(pinC, LOW);
  digitalWrite(pinD, LOW);
  digitalWrite(pinE, LOW);
  digitalWrite(pinF, LOW);
  digitalWrite(pinG, LOW);
  digitalWrite(pinH, LOW);
  digitalWrite(pinI, LOW);
  digitalWrite(pinJ, LOW);
  delay(subletspace);
}

void printX() {
  digitalWrite(pinJ, HIGH);
  digitalWrite(pinA, HIGH);
  delay(subletspace);
  digitalWrite(pinJ, LOW);
  digitalWrite(pinA, LOW);
  digitalWrite(pinI, HIGH);
  digitalWrite(pinB, HIGH);
  delay(subletspace);
  digitalWrite(pinI, LOW);
  digitalWrite(pinB, LOW);
  digitalWrite(pinH, HIGH);
  digitalWrite(pinC, HIGH);
  delay(subletspace);
  digitalWrite(pinH, LOW);
  digitalWrite(pinC, LOW);
  digitalWrite(pinG, HIGH);
  digitalWrite(pinD, HIGH);
  delay(subletspace);
  digitalWrite(pinG, LOW);
  digitalWrite(pinD, LOW);
  digitalWrite(pinF, HIGH);
  digitalWrite(pinE, HIGH);
  delay(subletspace*2);
  digitalWrite(pinF, LOW);
  digitalWrite(pinE, LOW);
  digitalWrite(pinG, HIGH);
  digitalWrite(pinD, HIGH);
  delay(subletspace);
  digitalWrite(pinG, LOW);
  digitalWrite(pinD, LOW);
  digitalWrite(pinH, HIGH);
  digitalWrite(pinC, HIGH);
  delay(subletspace);
  digitalWrite(pinH, LOW);
  digitalWrite(pinC, LOW);
  digitalWrite(pinI, HIGH);
  digitalWrite(pinB, HIGH);
  delay(subletspace);
  digitalWrite(pinI, LOW);
  digitalWrite(pinB, LOW);
  digitalWrite(pinJ, HIGH);
  digitalWrite(pinA, HIGH);
  delay(subletspace);
  digitalWrite(pinJ, LOW);
  digitalWrite(pinA, LOW);
  delay(subletspace);
  
}

void printY() {
  digitalWrite(pinJ, HIGH);
  delay(subletspace);
  digitalWrite(pinJ, LOW);
  digitalWrite(pinI, HIGH);
  delay(subletspace);
  digitalWrite(pinI, LOW);
  digitalWrite(pinH, HIGH);
  delay(subletspace);
  digitalWrite(pinH, LOW);
  digitalWrite(pinG, HIGH);
  delay(subletspace);
  digitalWrite(pinG, LOW);
  digitalWrite(pinF, HIGH);
  digitalWrite(pinE, HIGH);
  digitalWrite(pinD, HIGH);
  digitalWrite(pinC, HIGH);
  digitalWrite(pinB, HIGH);
  digitalWrite(pinA, HIGH);
  delay(subletspace);
  digitalWrite(pinF, LOW);
  digitalWrite(pinE, LOW);
  digitalWrite(pinD, LOW);
  digitalWrite(pinC, LOW);
  digitalWrite(pinB, LOW);
  digitalWrite(pinA, LOW);
  digitalWrite(pinG, HIGH);
  delay(subletspace);
  digitalWrite(pinG, LOW);
  digitalWrite(pinH, HIGH);
  delay(subletspace);
  digitalWrite(pinH, LOW);
  digitalWrite(pinI, HIGH);
  delay(subletspace);
  digitalWrite(pinI, LOW);
  digitalWrite(pinJ, HIGH);
  delay(subletspace);
  digitalWrite(pinJ, LOW);
  delay(subletspace);
  
}

void printZ() {
  digitalWrite(pinJ, HIGH);
  digitalWrite(pinB, HIGH);
  digitalWrite(pinA, HIGH);
  delay(subletspace);
  digitalWrite(pinB, LOW);
  digitalWrite(pinA, HIGH);
  digitalWrite(pinC, HIGH);
  digitalWrite(pinJ, HIGH);
  delay(subletspace);
  digitalWrite(pinC, LOW);
  digitalWrite(pinD, HIGH);
  delay(subletspace);
  digitalWrite(pinD, LOW);
  digitalWrite(pinE, HIGH);
  delay(subletspace);
  digitalWrite(pinE, LOW);
  digitalWrite(pinF, HIGH);
  delay(subletspace);
  digitalWrite(pinF, LOW);
  digitalWrite(pinG, HIGH);
  delay(subletspace);
  digitalWrite(pinG, LOW);
  digitalWrite(pinH, HIGH);
  delay(subletspace);
  digitalWrite(pinH, LOW);
  digitalWrite(pinI, HIGH);
  delay(subletspace);
  digitalWrite(pinI, LOW);
  digitalWrite(pinA, LOW);
  digitalWrite(pinJ, LOW);
  delay(subletspace);
  
}

void alphabet() {
  printA();
  delay(letspace);
  printB();
  delay(letspace);
  printC();
  delay(letspace);
  printD();
  delay(letspace);
  printE();
  delay(letspace);
  printF();
  delay(letspace);
  printG();
  delay(letspace);
  printE();
  delay(letspace);
  printF();
  delay(letspace);
  printG();
  delay(letspace);
  printH();
  delay(letspace);
  printI();
  delay(letspace);
  printJ();
  delay(letspace);
  printK();
  delay(letspace);
  printL();
  delay(letspace);
  printM();
  delay(letspace);
  printN();
  delay(letspace);
  printO();
  delay(letspace);
  printP();
  delay(letspace);
  printQ();
  delay(letspace);
  printR();
  delay(letspace);
  printS();
  delay(letspace);
  printT();
  delay(letspace);
  printU();
  delay(letspace);
  printV();
  delay(letspace);
  printW();
  delay(letspace);
  printX();
  delay(letspace);
  printY();
  delay(letspace);
  printZ();
  //now I know my ABCs
}

void loop() {
 alphabet();
  
}
